# Fritzing sketch Remote Wiring Diagram (saved by Fritzing 0.9.4)

parts:
  NodeMCU_V2 = NodeMCU V1.0
  TP4056 = TP4056 [chip_label=TP4056 package="DIP (Dual Inline) [THT]"]
  MT3608 = Mystery Part - 2 pins [chip_label=? package=THT]
  Joystick_left_x-Axis = Thumb Joystick
  Button_JS_left = Pushbutton [package="[THT]"]
  Button_1 = Round Pushbutton
  Switch_1 = Toggle Switch spst [package=THT]
  ADS1115 = ADS1115
  ADS1115_2 = ADS1115
  3_7V_2000mAh_LiPo = LiPoly Battery (1300mAh)
  Power_Switch = Toggle Switch spst [package=THT]
  Switch_2 = Toggle Switch spst [package=THT]
  Switch_3 = Toggle Switch spst [package=THT]
  Switch_4 = Toggle Switch spst [package=THT]
  Switch_5 = Toggle Switch spst [package=THT]
  Button_3 = Round Pushbutton
  Button_4 = Round Pushbutton
  MCP23017 = MCP23017 I2C I/O Expander
  R1 = Resistor [tolerance=±5% resistance=1k package=THT]
  LED1 = LED - 5mm [color="Green (555nm)" package="5 mm [THT]"]
  Button_2 = Round Pushbutton
  LED2 = LED - 5mm [color="Green (555nm)" package="5 mm [THT]"]
  LED3 = LED - 5mm [color="Green (555nm)" package="5 mm [THT]"]
  LED4 = LED - 5mm [color="Green (555nm)" package="5 mm [THT]"]
  LED5 = LED - 5mm [color="Green (555nm)" package="5 mm [THT]"]
  R2 = Resistor [tolerance=±5% resistance=1k package=THT]
  R3 = Resistor [tolerance=±5% resistance=1k package=THT]
  R4 = Resistor [tolerance=±5% resistance=1k package=THT]
  R5 = Resistor [tolerance=±5% resistance=1k package=THT]
  Joystick_left_y-Axis = Thumb Joystick
  Joystick_left_z-Axis = Thumb Joystick
  Joystick_right_x-Axis = Thumb Joystick
  Joystick_right_z-Axis = Thumb Joystick
  Joystick_right_y-Axis = Thumb Joystick
  Button_JS_right = Pushbutton [package="[THT]"]
  Bauteil1 = NRF24L01+ Breakout Board

nets:
  N1: NodeMCU_V2.D0, Bauteil1.CS
  N2: NodeMCU_V2.D1, ADS1115.SCL, ADS1115_2.SCL, MCP23017.SCL
  N3: NodeMCU_V2.D2, ADS1115.SDA, ADS1115_2.SDA, MCP23017.SDA
  N4: NodeMCU_V2.D4, Bauteil1.CE
  3V3: NodeMCU_V2.3V3, Bauteil1.VCC
  GND: NodeMCU_V2.GND, MT3608.VOUT-, Joystick_left_x-Axis.GND, Button_JS_left.Pin_2, Button_1.leg0, Switch_1.L1, ADS1115.GND, ADS1115.ADDR, ADS1115_2.GND, Switch_2.L1, Switch_3.L1, Switch_4.L1, Switch_5.L1, Button_3.leg1, Button_4.leg1, MCP23017.VSS, LED1.cathode, Button_2.leg0, LED2.cathode, LED3.cathode, LED4.cathode, LED5.cathode, Joystick_left_y-Axis.GND, Joystick_left_z-Axis.GND, Joystick_right_x-Axis.GND, Joystick_right_z-Axis.GND, Joystick_right_y-Axis.GND, Button_JS_right.Pin_1, Button_JS_right.Pin_2, Bauteil1.GND
  N5: NodeMCU_V2.D5, Bauteil1.SCK
  N6: NodeMCU_V2.D6, Bauteil1.MISO
  N7: NodeMCU_V2.D7, Bauteil1.MOSI
  VCC: NodeMCU_V2.Vin, MT3608.VOUT+, Joystick_left_x-Axis.VCC, ADS1115.VDD, ADS1115_2.VDD, ADS1115_2.ADDR, MCP23017.VDD, Joystick_left_y-Axis.VCC, Joystick_left_z-Axis.VCC, Joystick_right_x-Axis.VCC, Joystick_right_z-Axis.VCC, Joystick_right_y-Axis.VCC
  N8: TP4056.pin3, Power_Switch.L1
  N9: TP4056.pin4, 3_7V_2000mAh_LiPo.positive
  N10: TP4056.pin5, 3_7V_2000mAh_LiPo.negative
  N11: TP4056.pin6, MT3608.VIN-
  N12: MT3608.VIN+, Power_Switch.COM
  N13: Joystick_left_x-Axis.VERT, ADS1115.A1
  N14: Button_JS_left.Pin_3, Button_JS_left.Pin_4, MCP23017.GPB7
  N15: Button_1.leg1, MCP23017.GPA1
  N16: Switch_1.COM, MCP23017.GPB0
  N17: ADS1115.A2, Joystick_left_y-Axis.VERT
  N18: ADS1115.A3, Joystick_left_z-Axis.VERT
  N19: ADS1115_2.A1, Joystick_right_x-Axis.VERT
  N20: ADS1115_2.A2, Joystick_right_y-Axis.VERT
  N21: ADS1115_2.A3, Joystick_right_z-Axis.VERT
  N22: Switch_2.COM, MCP23017.GPB1
  N23: Switch_3.COM, MCP23017.GPB2
  N24: Switch_4.COM, MCP23017.GPB3
  N25: Switch_5.COM, MCP23017.GPB4
  N26: Button_3.leg0, MCP23017.GPB5
  N27: Button_4.leg0, MCP23017.GPB6
  N28: MCP23017.GPA0, Button_JS_right.Pin_3
  N29: MCP23017.GPA2, Button_2.leg1
  N30: MCP23017.GPA3, R5.Pin_0
  N31: MCP23017.GPA4, R4.Pin_0
  N32: MCP23017.GPA5, R3.Pin_0
  N33: MCP23017.GPA6, R2.Pin_0
  N34: MCP23017.GPA7, R1.Pin_0
  N35: R1.Pin_1, LED1.anode
  N36: LED2.anode, R2.Pin_1
  N37: LED3.anode, R3.Pin_1
  N38: LED4.anode, R4.Pin_1
  N39: LED5.anode, R5.Pin_1

custom parts:
  NodeMCU V1.0: ESP8266 based NodeMCU
  TP4056: A DIP stand-in part for whatever IC you want. With 6 pins on a 300mil dual inline package (DIP) footprint.
  Mystery Part - 2 pins: A dummy, proxy, ersatz, stand-in part for whatever you want. With 2 pins on a 100 mil inline pin header footprint.
  Toggle Switch spst: Toggle Switch single pole single throw
  ADS1115: ADC ADS1115
  LiPoly Battery (1300mAh): Lithium Ion Polymer Battery (1300mAh)
  MCP23017 I2C I/O Expander: The MCP23017 uses two i2c pins (these can be shared with other i2c devices), and in exchange gives you 16 general purpose pins. You can set each of 16 pins to be input, output, input with a pullup or open drain. There's even the ability to get an interrupt via an external pin when any of the inputs change so you don't have to keep polling the chip.
